# Fritzing sketch Protoboard (saved by Fritzing 0.9.3b)
breadboards: 1

parts:
  U1 = attiny85 [package=dip]
  RHT1 = Humidity and Temperature Sensor RHT03
  Componente1 = Bluetooth HC-05 Macho
  Componente2 = ws2812b [package="smd 2812b"]

nets:
  N1: U1.Pin_2, RHT1.Data-signal
  N2: U1.Pin_3, Componente2.DIN
  N3: U1.Pin_4, Componente1.GND
  N4: U1.Pin_6, Componente1.RXD
  N5: U1.Pin_7, Componente1.TXD
  N6: U1.Pin_8, RHT1.Vcc
  N7: RHT1.GND_2, Componente2.VSS
  VCC: Componente1.VCC, Componente2.VDD
